// Digital circuit core.dig as structural Verilog
module core (
  input  clk,
  output [31:0] out
);

  wire [31:0] pc_1_out, sum_s;

  PC pc_1 (.in(sum_s), .clk(clk), .out(pc_1_out));
  Add #(.Bits(32)) sum (.a(pc_1_out), .b(32'h4), .c_i(1'b0), .s(sum_s));  // open: c_o
  Insts_Memory insts_memory_1 (.pc(pc_1_out));  // open: out
  control_unit control_unit_1 ();  // open: instr
endmodule
